// Digital circuit cpu.dig as structural Verilog
module cpu (
  input  clk,
  output [31:0] ReadData1,
  output [31:0] ReadData2
);

  wire [2:0] funct3;
  wire [4:0] rd, rs1, rs2;
  wire [6:0] funct7, opcode;
  wire [15:0] immediate;
  wire [31:0] add_1_s, PC_q;

  Multiplexer multiplexer_1 ();  // open: sel, in_0, in_1, out
  // alu alu_1: pin names not known
  control_unit control_unit_1 ();  // open: opcode, funct3, funct7, ALUOp, ImmSrc, ALUSrc, RegWrite
  Register #(.Bits(32), .isProgramCounter("true")) PC (.D(add_1_s), .C(clk), .en(1'b1), .Q(PC_q));
  Add #(.Bits(32)) add_1 (.a(32'h4), .b(PC_q), .c_i(1'b0), .s(add_1_s));  // open: c_o
  ROM #(.AddrBits(10), .isProgramMemory("true"), .Bits(32)) Instruction_Memory (
    .A(PC_q[11:2]), .sel(1'b1), .D({funct7, rs2, rs1, funct3, rd, opcode}));
  BitExtender bitextender_1 (.in({funct7[2:0], rs2}), .out(immediate));
  // Pins of 8 and 12 bits meet at {funct7, rs2}

  // Other names for the same wires on the sheet: clock = clk

  // Notes on the sheet:
  //   Instruction_Memory loads imem.mem
endmodule

/* Test case cpu:
clk ReadData1 ReadData2
*/
